# Fritzing sketch Project4 (saved by Fritzing 0.8.7b)
breadboards: 1

parts:
  S1 = Pushbutton [package="[THT]"]
  R1 = Resistor [tolerance=±5% resistance=1k package=THT]
  LED1 = LED - 5mm [color="Red (633nm)" package="5 mm [THT]"]
  Part1 = Arduino Uno (Rev3)

nets:
  N1: S1.Pin_1, S1.Pin_2, R1.Pin_0, Part1.D2
  N2: S1.Pin_3, S1.Pin_4, Part1.5V
  N3: R1.Pin_1, LED1.cathode, Part1.GND
  N4: LED1.anode, Part1.D11_PWM/MOSI

notes:
  D2
  D11
