# Fritzing sketch Project5 (saved by Fritzing 0.8.7b)
breadboards: 1

parts:
  R1 = Resistor [tolerance=±5% resistance=1k package=THT]
  LED1 = LED - 5mm [color="Red (633nm)" package="5 mm [THT]"]
  Part1 = Arduino Uno (Rev3)
  R2 = Photocell (LDR) [package=THT]

nets:
  N1: R1.Pin_1, Part1.5V
  N2: LED1.cathode, Part1.GND
  N3: LED1.anode, Part1.D11_PWM/MOSI
  N4: Part1.D2, R2.pin_0

notes:
  D2
  D11
