# Fritzing sketch Project6 (saved by Fritzing 0.8.7b)
breadboards: 1

parts:
  Part1 = Arduino Uno (Rev3)
  U1 = POT [package=pot_mammoth]
  LED1 = LED - 5mm [color="White (4500K)" package="5 mm [THT]"]

nets:
  N1: Part1.A0, U1.A
  N2: Part1.D11_PWM/MOSI, LED1.anode
  N3: Part1.GND, LED1.cathode
  N4: Part1.5V, U1.S, U1.E

notes:
  D11
